# Fritzing sketch Gauntlet_V2 (saved by Fritzing 0.9.3b)
breadboards: 1

parts:
  Q3 = NPN-Transistor [package="TO92 [THT]"]
  Q5 = NPN-Transistor [package="TO92 [THT]"]
  D5 = Rectifier Diode [part_number=1N4001 package="300 mil [THT]"]
  D4 = Rectifier Diode [part_number=1N4001 package="300 mil [THT]"]
  R16 = Resistor [tolerance=±5% resistance=220 package=THT]
  R18 = Resistor [tolerance=±5% resistance=220 package=THT]
  R19 = Resistor [tolerance=±5% resistance=220 package=THT]
  Q4 = NPN-Transistor [package="TO92 [THT]"]
  MOTOR2 = Vibration Motor
  MOTOR5 = Vibration Motor
  Q1 = NPN-Transistor [package="TO92 [THT]"]
  R17 = Resistor [tolerance=±5% resistance=220 package=THT]
  MOTOR3 = Vibration Motor
  MOTOR1 = Vibration Motor
  Part2 = 12 NeoPixel Ring [part_number=1643]
  MOTOR4 = Vibration Motor
  R15 = Resistor [tolerance=±10% resistance=220 package=THT]
  Q2 = NPN-Transistor [package="TO92 [THT]"]
  D3 = Rectifier Diode [part_number=1N4001 package="300 mil [THT]"]
  R9 = Resistor [tolerance=±5% resistance=10k package=THT]
  D1 = Rectifier Diode [part_number=1N4001 package="300 mil [THT]"]
  R3 = Basic Flex Resistor
  R6 = Resistor [tolerance=±5% resistance=10k package=THT]
  Part1 = Adafruit Feather M0 Bluefruit LE [part_number="Adafruit #2995"]
  R7 = Resistor [tolerance=±5% resistance=10k package=THT]
  R4 = Basic Flex Resistor
  R8 = Resistor [tolerance=±5% resistance=10k package=THT]
  R1 = Basic Flex Resistor
  R2 = Basic Flex Resistor
  R5 = Basic Flex Resistor
  R10 = Resistor [tolerance=±5% resistance=10k package=THT]
  D6 = Rectifier Diode [part_number=1N4001 package="300 mil [THT]"]

nets:
  GND: Q3.E, Q5.E, Q4.E, Q1.E, Part2.GND, Q2.E, R3.pin_1, R4.pin_1, R1.pin_1, R2.pin_1, R5.pin_1
  N1: Q3.B, R17.Pin_1
  N2: Q3.C, MOTOR3.NEG, D3.anode
  N3: Q5.B, R19.Pin_1
  N4: Q5.C, D5.anode, MOTOR5.NEG
  5V: D5.cathode, D4.cathode, MOTOR2.POS, MOTOR5.POS, Part2.VDD, MOTOR4.POS, R9.Pin_1, R6.Pin_1, R7.Pin_1, R8.Pin_1, R10.Pin_1, D6.cathode
  N5: D4.anode, Q4.C, MOTOR4.NEG
  N6: R16.Pin_0, Part1.D6
  N7: R16.Pin_1, Q2.B
  N8: R18.Pin_0, Part1.D11
  N9: R18.Pin_1, Q4.B
  N10: R19.Pin_0, Part1.D12
  N11: MOTOR2.NEG, Q2.C, D6.anode
  N12: Q1.B, R15.Pin_0
  N13: Q1.C, MOTOR1.NEG, D1.anode
  N14: R17.Pin_0, Part1.D10
  N15: MOTOR3.POS, D3.cathode
  N16: MOTOR1.POS, D1.cathode
  N17: Part2.IN, Part1.D13
  N18: R15.Pin_1, Part1.D5
  N19: R9.Pin_0, Part1.A3, R4.Pin_2
  N20: R3.Pin_2, Part1.A2, R8.Pin_0
  N21: R6.Pin_0, Part1.A0, R1.Pin_2
  N22: Part1.A4, R5.Pin_2, R10.Pin_0
  N23: Part1.A1, R7.Pin_0, R2.Pin_2

custom parts:
  Vibration Motor: An eccentric vibration motor!
  12 NeoPixel Ring: 12 ultra bright smart LED NeoPixels are arranged in a circle with 1.5" (37mm) outer diameter. The rings are 'chainable' - connect the output pin of one to the input pin of another. Use only one microcontroller pin to control as many as you can chain together! Each LED is addressable as the driver chip is inside the LED. Each one has ~18mA constant current drive so the color will be very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
  Adafruit Feather M0 Bluefruit LE: This is the Adafruit Feather M0 Bluefruit LE - our take on an 'all-in-one' Arduino-compatible + Bluetooth Low Energy with built in USB and battery charging. Its an Adafruit Feather M0 with a BTLE module, ready to rock! We have other boards in the Feather family, check'em out here. Bluetooth Low Energy is the hottest new low-power, 2.4GHz spectrum wireless protocol. In particular, its the only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
